# Fritzing sketch motor paso a paso (saved by Fritzing 0.9.3b)
breadboards: 1

parts:
  Componente1 = Arduino Uno (Rev3)
  Pololu_A1 = Pololu A4988 [package=SO16]
  M1 = Stepper Motor - Bipolar
  Power_plug1 = Power plug
  S1 = Pushbutton [package="[THT]"]

nets:
  N1: Componente1.D10_PWM/SS, S1.Pin_3, S1.Pin_4
  N2: Componente1.D4, Pololu_A1.STEP
  N3: Componente1.D5_PWM, Pololu_A1.DIR
  5V: Componente1.5V, Pololu_A1.VDD
  N4: Componente1.GND, Pololu_A1.GND#8, S1.Pin_1, S1.Pin_2
  N5: Pololu_A1.RESET, Pololu_A1.SLEEP
  N6: Pololu_A1.1B, M1.D
  N7: Pololu_A1.1A, M1.B
  N8: Pololu_A1.2A, M1.C
  N9: Pololu_A1.2B, M1.A
  N10: Pololu_A1.GND#14, Power_plug1.GND
  N11: Pololu_A1.VMOT, Power_plug1.VCC

notes:
  micro switch de final de carrera
  al ic conversor de dmx a arduino
  A4588 driver
